// Logisim project cpu.circ as structural Verilog: 1 circuit, main circuit main
module main (
  input  [31:0] INSTRUCTION,
  input  CLOCK,
  output [31:0] FETCH_ADDRESS,
  output [31:0] R0_Value,
  output [31:0] R1_Value,
  output [31:0] R2_Value,
  output [31:0] LR_Value,
  output [31:0] SP_Value
);

  wire main_1_p1, main_1_p2, main_1_p3, main_1_p7, main_1_p8, main_1_p10, main_1_p17, main_1_p18, main_1_p19;
  wire [31:0] main_1_p4, main_1_p14, main_1_p15, main_1_p16, multiplexer_1_out;

  Register #(.width(32)) PC ();  // open: D, en, Q, clk, clr
  // regfile_main main_1: pin names not known; wires that end beside it: main_1_p1, main_1_p2, main_1_p3, main_1_p4, R0_Value, R1_Value, main_1_p7, main_1_p8, main_1_p8, main_1_p10, R2_Value, LR_Value, SP_Value, main_1_p14, main_1_p15, main_1_p16, main_1_p17, main_1_p18, main_1_p19
  Multiplexer #(.width(32), .enable("false")) multiplexer_1 (
    .in0(main_1_p15), .in1(main_1_p16), .out(multiplexer_1_out), .sel(main_1_p17));
  Adder #(.width(32)) adder_1 (.a(main_1_p14), .b(multiplexer_1_out), .out(main_1_p4));  // open: cin, cout

  // Other names for the same wires on the sheet: clk = CLOCK; fetch_addr[31:0] = FETCH_ADDRESS; R0[31:0] = R0_Value;
  //   R1[31:0] = R1_Value; R2[31:0] = R2_Value; R13[31:0] = SP_Value; R14[31:0] = LR_Value

  // Notes on the sheet:
  //   Output
  //   Rn
  //   Rm
  //   Rd
  //   Inputs
  //   Immediate
  //   I
  //   These are DEBUG/TEST outputs from your circuit.
endmodule
